# Fritzing sketch mbed-motor-circuit (saved by Fritzing 0.6.3b)
stripboards: 1

parts:
  IC1 = H-Bridge [part_number=L293D package=THT]
  J2 = Screw terminal - 2 pins [part_number="Motor 1" package=THT]
  J3 = Screw terminal - 2 pins [part_number="Motor Power" package=THT]
  J4 = Screw terminal - 2 pins [part_number="Motor 2" package=THT]
  D1 = Rectifier Diode [part_number=1N4001 package="300 mil [THT]"]

nets:
  N1: IC1.1Y, J2.pin1
  GND1: IC1.GND1, IC1.GND4, D1.anode
  GND2: IC1.GND2, IC1.GND3
  N2: IC1.2Y, J2.pin2
  N3: IC1.3Y, J4.pin1
  N4: IC1.4Y, J4.pin2
  N5: IC1.VCC1, J3.pin2
  N6: J3.pin1, D1.cathode
